# Fritzing sketch GarageParkingAssistant (saved by Fritzing 0.9.10b)

parts:
  Power_12_Volts = Power plug
  Arduino_Nano1 = Arduino Nano (Rev3.0)
  LCD2004-I2C1 = LCD2004-I2C  # not connected
  Part1 = SRF05 Ultrasonic Rangefinder  # not connected
  Part2 = SRF05 Ultrasonic Rangefinder  # not connected
  AM1 = AM2302 Humidity and Temperature Sensor  # not connected
  U1 = WS2812 RGB LED strip
  U2 = WS2812 RGB LED strip  # not connected
  U3 = WS2812 RGB LED strip  # not connected
  U4 = WS2812 RGB LED strip  # not connected
  IC1 = Voltage Regulator [package=78xxl]

nets:
  GND: Power_12_Volts.GND, Arduino_Nano1.GND, IC1.GND
  VCC: Power_12_Volts.VCC, Arduino_Nano1.VIN, IC1.IN
  N1: U1.VCC, IC1.OUT

custom parts:
  LCD2004-I2C: A standard character display with 4x20 characters. Comes in many colors with LCM2004 IIC attached.
  WS2812 RGB LED strip: WS2812 strip
